// Logisim project circ.circ as structural Verilog: 1 circuit, main circuit main
module main (
);

  wire adder_1_cout, and_1_out, button_1_out, clock_1_out, decoder_1_out0, decoder_1_out1, decoder_1_out2,
       decoder_1_out3, decoder_1_out4, decoder_1_out5, decoder_1_out6, decoder_1_out7, decoder_1_out8,
       decoder_1_out9, decoder_1_out10, decoder_1_out11, decoder_1_out12, decoder_1_out13, decoder_1_out14,
       decoder_1_out15, not_1_out, not_2_out, or_1_out, or_5_out, or_7_out, or_9_out, or_11_out, or_13_out,
       or_15_out, or_17_out, or_19_out, or_21_out, or_23_out, or_25_out, or_27_out, or_29_out, or_31_out,
       or_33_out, or_35_out, subtractor_1_bout;
  wire [2:0] or_3_out;
  wire [3:0] register_4_q_2, register_5_q, register_5_q_2, register_5_q_3, register_5_q_4, rom_1_data_2;
  wire [6:0] register_1_q;
  wire [10:0] register_2_q, register_3_q;
  wire [15:0] adder_1_out, and_2_out, button_17_out, controlled_buffer_1_out, counter_1_q, decoder_2_out15,
       divider_1_out, multiplexer_1_out, multiplier_1_out, not_3_out, or_2_out, or_4_out, or_6_out, or_8_out,
       or_10_out, or_12_out, or_14_out, or_16_out, or_18_out, or_20_out, or_22_out, or_24_out, or_26_out,
       or_28_out, or_30_out, or_32_out, or_34_out, ram_1_dout, register_6_q, register_7_q, register_8_q,
       register_9_q, register_10_q, register_11_q, register_12_q, register_13_q, register_14_q,
       register_15_q, register_16_q, register_17_q, register_18_q, register_19_q, register_20_q,
       register_21_q, shifter_1_out, shifter_2_out, subtractor_1_out, xor_1_out;
  wire [15:4] register_4_q;
  wire [15:7] register_1_q_2;
  wire [21:0] rom_1_data;

  ROM #(.addrWidth(11), .dataWidth(22)) rom_1 (
    .addr(register_2_q), .data({rom_1_data[21:10], rom_1_data_2, rom_1_data[5:0]}));
  Register #(.width(16)) register_1 (
    .D(controlled_buffer_1_out), .en(rom_1_data[17]), .Q({register_1_q_2, register_1_q}), .clk(and_1_out),
    .clr(button_1_out));
  Register #(.width(3)) register_2 (
    .D(or_3_out), .en(rom_1_data[16]), .Q(register_2_q[10:8]), .clk(and_1_out), .clr(button_1_out));
  Register #(.width(16)) register_3 (
    .D(controlled_buffer_1_out), .en(rom_1_data[15]), .Q({register_2_q[7:3], register_3_q}), .clk(and_1_out),
    .clr(button_1_out));
  Register #(.width(16)) register_4 (
    .D(controlled_buffer_1_out), .en(rom_1_data[21]), .Q({register_4_q, register_4_q_2}), .clk(and_1_out),
    .clr(button_1_out));
  Counter #(.max('hffff), .width(16)) counter_1 (
    .load(rom_1_data[13]), .D(controlled_buffer_1_out), .count(rom_1_data[11]), .Q(counter_1_q),
    .clk(and_1_out), .clr(button_1_out));  // open: carry, up
  assign controlled_buffer_1_out = rom_1_data[19] ? {register_4_q, register_4_q_2} : 16'bz;  // Controlled_Buffer controlled_buffer_1
  assign controlled_buffer_1_out = rom_1_data[14] ? {{5{1'b0}}, register_3_q} : 16'bz;  // Controlled_Buffer controlled_buffer_2
  assign controlled_buffer_1_out = rom_1_data[12] ? counter_1_q : 16'bz;  // Controlled_Buffer controlled_buffer_3
  assign controlled_buffer_1_out = rom_1_data[18] ? {register_5_q_3, register_5_q_2, register_5_q, register_5_q_4} : 16'bz;  // Controlled_Buffer controlled_buffer_4
  Register #(.width(16)) register_5 (
    .D(controlled_buffer_1_out), .en(rom_1_data[20]),
    .Q({register_5_q_3, register_5_q_2, register_5_q, register_5_q_4}), .clk(and_1_out), .clr(button_1_out));
  Counter #(.max('h7), .width(3)) counter_2 (
    .Q(register_2_q[2:0]), .clk(not_1_out), .clr(or_1_out));  // open: load, D, count, carry, up
  not not_1 (not_1_out, and_1_out);
  or or_1 (or_1_out, rom_1_data[10], button_1_out);
  Clock clock_1 (.out(clock_1_out));
  not not_2 (not_2_out, button_1_out);
  and and_1 (and_1_out, clock_1_out, not_2_out);
  Adder #(.width(16)) adder_1 (
    .a({register_4_q, register_4_q_2}), .b({register_5_q_3, register_5_q_2, register_5_q, register_5_q_4}),
    .out(adder_1_out), .cout(adder_1_cout));  // open: cin
  Subtractor #(.width(16)) subtractor_1 (
    .a({register_4_q, register_4_q_2}), .b({register_5_q_3, register_5_q_2, register_5_q, register_5_q_4}),
    .out(subtractor_1_out), .bout(subtractor_1_bout));  // open: bin
  Multiplier #(.width(16)) multiplier_1 (
    .a({register_4_q, register_4_q_2}), .b({register_5_q_3, register_5_q_2, register_5_q, register_5_q_4}),
    .out(multiplier_1_out));  // open: cin, cout
  Divider #(.width(16)) divider_1 (
    .a({register_4_q, register_4_q_2}), .b({register_5_q_3, register_5_q_2, register_5_q, register_5_q_4}),
    .out(divider_1_out));  // open: upper, rem
  Shifter #(.width(16)) shifter_1 (.in({register_4_q, register_4_q_2}), .\dist (register_5_q_4), .out(shifter_1_out));
  Shifter #(.shift("lr"), .width(16)) shifter_2 (
    .in({register_4_q, register_4_q_2}), .\dist (register_5_q_4), .out(shifter_2_out));
  assign not_3_out = ~{register_4_q, register_4_q_2};  // NOT_Gate not_3, 16 bits wide
  assign and_2_out = {register_4_q, register_4_q_2} & {register_5_q_3, register_5_q_2, register_5_q, register_5_q_4};  // AND_Gate and_2, 16 bits wide
  assign or_2_out = {register_4_q, register_4_q_2} | {register_5_q_3, register_5_q_2, register_5_q, register_5_q_4};  // OR_Gate or_2, 16 bits wide
  assign xor_1_out = {register_4_q, register_4_q_2} ^ {register_5_q_3, register_5_q_2, register_5_q, register_5_q_4};  // XOR_Gate xor_1, 16 bits wide
  or or_3 (or_3_out[0], adder_1_cout, subtractor_1_bout);
  Multiplexer #(.select(4), .width(16)) multiplexer_1 (
    .in0(adder_1_out), .in1(subtractor_1_out), .in2(multiplier_1_out), .in3(divider_1_out),
    .in4(shifter_1_out), .in5(shifter_2_out), .in6(not_3_out), .in7(and_2_out), .in8(or_2_out),
    .in9(xor_1_out), .out(multiplexer_1_out));  // open: in10, in11, in12, in13, in14, in15, sel
  assign controlled_buffer_1_out = rom_1_data[5] ? multiplexer_1_out : 16'bz;  // Controlled_Buffer controlled_buffer_5
  RAM #(.addrWidth(7), .dataWidth(16), .enables("line")) ram_1 (
    .addr(register_1_q), .we(rom_1_data[4]), .clk(and_1_out), .din(controlled_buffer_1_out), .dout(ram_1_dout));
  Button button_1 (.out(button_1_out));
  Button button_2 (.out(button_17_out[15]));
  Button button_3 (.out(button_17_out[14]));
  Button button_4 (.out(button_17_out[13]));
  Button button_5 (.out(button_17_out[12]));
  Button button_6 (.out(button_17_out[11]));
  Comparator #(.width(16)) comparator_1 (
    .a({register_4_q, register_4_q_2}), .b({16{1'b0}}), .eq(or_3_out[1]));  // open: gt, lt
  Comparator #(.width(16)) comparator_2 (
    .a({register_4_q, register_4_q_2}), .b({register_5_q_3, register_5_q_2, register_5_q, register_5_q_4}),
    .eq(or_3_out[2]));  // open: gt, lt
  Button button_7 (.out(button_17_out[10]));
  Button button_8 (.out(button_17_out[9]));
  Button button_9 (.out(button_17_out[8]));
  Button button_10 (.out(button_17_out[7]));
  assign controlled_buffer_1_out = rom_1_data[2] ? button_17_out : 16'bz;  // Controlled_Buffer controlled_buffer_6
  DotMatrix #(.matrixcols(16), .matrixrows(16)) dotmatrix_1 (
    .col0(register_6_q), .col1(register_8_q), .col2(register_10_q), .col3(register_12_q),
    .col4(register_14_q), .col5(register_16_q), .col6(register_18_q), .col7(register_20_q),
    .col8(register_7_q), .col9(register_9_q), .col10(register_11_q), .col11(register_13_q),
    .col12(register_15_q), .col13(register_17_q), .col14(register_19_q), .col15(register_21_q));
  assign controlled_buffer_1_out = rom_1_data[3] ? ram_1_dout : 16'bz;  // Controlled_Buffer controlled_buffer_7
  Button button_11 (.out(button_17_out[6]));
  Button button_12 (.out(button_17_out[5]));
  Button button_13 (.out(button_17_out[4]));
  Button button_14 (.out(button_17_out[3]));
  Button button_15 (.out(button_17_out[2]));
  Button button_16 (.out(button_17_out[1]));
  Button button_17 (.out(button_17_out[0]));
  assign or_4_out = register_6_q | decoder_2_out15;  // OR_Gate or_4, 16 bits wide
  or or_5 (or_5_out, rom_1_data[1], button_1_out);
  assign or_6_out = register_7_q | decoder_2_out15;  // OR_Gate or_6, 16 bits wide
  or or_7 (or_7_out, rom_1_data[1], button_1_out);
  Decoder #(.select(4)) decoder_1 (
    .out0(decoder_1_out0), .out1(decoder_1_out1), .out2(decoder_1_out2), .out3(decoder_1_out3),
    .out4(decoder_1_out4), .out5(decoder_1_out5), .out6(decoder_1_out6), .out7(decoder_1_out7),
    .out8(decoder_1_out8), .out9(decoder_1_out9), .out10(decoder_1_out10), .out11(decoder_1_out11),
    .out12(decoder_1_out12), .out13(decoder_1_out13), .out14(decoder_1_out14), .out15(decoder_1_out15),
    .sel(register_4_q_2), .en(rom_1_data[0]));
  Register #(.width(16)) register_6 (
    .D(or_4_out), .en(decoder_1_out0), .Q(register_6_q), .clk(and_1_out), .clr(or_5_out));
  Register #(.width(16)) register_7 (
    .D(or_6_out), .en(decoder_1_out8), .Q(register_7_q), .clk(and_1_out), .clr(or_7_out));
  assign or_8_out = register_8_q | decoder_2_out15;  // OR_Gate or_8, 16 bits wide
  or or_9 (or_9_out, rom_1_data[1], button_1_out);
  assign or_10_out = register_9_q | decoder_2_out15;  // OR_Gate or_10, 16 bits wide
  or or_11 (or_11_out, rom_1_data[1], button_1_out);
  Register #(.width(16)) register_8 (
    .D(or_8_out), .en(decoder_1_out1), .Q(register_8_q), .clk(and_1_out), .clr(or_9_out));
  Register #(.width(16)) register_9 (
    .D(or_10_out), .en(decoder_1_out9), .Q(register_9_q), .clk(and_1_out), .clr(or_11_out));
  assign or_12_out = register_10_q | decoder_2_out15;  // OR_Gate or_12, 16 bits wide
  Register #(.width(16)) register_10 (
    .D(or_12_out), .en(decoder_1_out2), .Q(register_10_q), .clk(and_1_out), .clr(or_13_out));
  or or_13 (or_13_out, rom_1_data[1], button_1_out);
  assign or_14_out = register_11_q | decoder_2_out15;  // OR_Gate or_14, 16 bits wide
  Register #(.width(16)) register_11 (
    .D(or_14_out), .en(decoder_1_out10), .Q(register_11_q), .clk(and_1_out), .clr(or_15_out));
  or or_15 (or_15_out, rom_1_data[1], button_1_out);
  assign or_16_out = register_12_q | decoder_2_out15;  // OR_Gate or_16, 16 bits wide
  or or_17 (or_17_out, rom_1_data[1], button_1_out);
  assign or_18_out = register_13_q | decoder_2_out15;  // OR_Gate or_18, 16 bits wide
  or or_19 (or_19_out, rom_1_data[1], button_1_out);
  Register #(.width(16)) register_12 (
    .D(or_16_out), .en(decoder_1_out3), .Q(register_12_q), .clk(and_1_out), .clr(or_17_out));
  Register #(.width(16)) register_13 (
    .D(or_18_out), .en(decoder_1_out11), .Q(register_13_q), .clk(and_1_out), .clr(or_19_out));
  assign or_20_out = register_14_q | decoder_2_out15;  // OR_Gate or_20, 16 bits wide
  or or_21 (or_21_out, rom_1_data[1], button_1_out);
  assign or_22_out = register_15_q | decoder_2_out15;  // OR_Gate or_22, 16 bits wide
  or or_23 (or_23_out, rom_1_data[1], button_1_out);
  Register #(.width(16)) register_14 (
    .D(or_20_out), .en(decoder_1_out4), .Q(register_14_q), .clk(and_1_out), .clr(or_21_out));
  Register #(.width(16)) register_15 (
    .D(or_22_out), .en(decoder_1_out12), .Q(register_15_q), .clk(and_1_out), .clr(or_23_out));
  assign or_24_out = register_16_q | decoder_2_out15;  // OR_Gate or_24, 16 bits wide
  or or_25 (or_25_out, rom_1_data[1], button_1_out);
  assign or_26_out = register_17_q | decoder_2_out15;  // OR_Gate or_26, 16 bits wide
  or or_27 (or_27_out, rom_1_data[1], button_1_out);
  Register #(.width(16)) register_16 (
    .D(or_24_out), .en(decoder_1_out5), .Q(register_16_q), .clk(and_1_out), .clr(or_25_out));
  Register #(.width(16)) register_17 (
    .D(or_26_out), .en(decoder_1_out13), .Q(register_17_q), .clk(and_1_out), .clr(or_27_out));
  assign or_28_out = register_18_q | decoder_2_out15;  // OR_Gate or_28, 16 bits wide
  Register #(.width(16)) register_18 (
    .D(or_28_out), .en(decoder_1_out6), .Q(register_18_q), .clk(and_1_out), .clr(or_29_out));
  or or_29 (or_29_out, rom_1_data[1], button_1_out);
  assign or_30_out = register_19_q | decoder_2_out15;  // OR_Gate or_30, 16 bits wide
  Register #(.width(16)) register_19 (
    .D(or_30_out), .en(decoder_1_out14), .Q(register_19_q), .clk(and_1_out), .clr(or_31_out));
  or or_31 (or_31_out, rom_1_data[1], button_1_out);
  assign or_32_out = register_20_q | decoder_2_out15;  // OR_Gate or_32, 16 bits wide
  or or_33 (or_33_out, rom_1_data[1], button_1_out);
  assign or_34_out = register_21_q | decoder_2_out15;  // OR_Gate or_34, 16 bits wide
  or or_35 (or_35_out, rom_1_data[1], button_1_out);
  Register #(.width(16)) register_20 (
    .D(or_32_out), .en(decoder_1_out7), .Q(register_20_q), .clk(and_1_out), .clr(or_33_out));
  Register #(.width(16)) register_21 (
    .D(or_34_out), .en(decoder_1_out15), .Q(register_21_q), .clk(and_1_out), .clr(or_35_out));
  Decoder #(.enable("false"), .select(4)) decoder_2 (
    .out0(decoder_2_out15[15]), .out1(decoder_2_out15[14]), .out2(decoder_2_out15[13]),
    .out3(decoder_2_out15[12]), .out4(decoder_2_out15[11]), .out5(decoder_2_out15[10]),
    .out6(decoder_2_out15[9]), .out7(decoder_2_out15[8]), .out8(decoder_2_out15[7]),
    .out9(decoder_2_out15[6]), .out10(decoder_2_out15[5]), .out11(decoder_2_out15[4]),
    .out12(decoder_2_out15[3]), .out13(decoder_2_out15[2]), .out14(decoder_2_out15[1]),
    .out15(decoder_2_out15[0]), .sel(register_5_q_4));

  // Notes on the sheet:
  //   contents of rom_1 (hex, n*v repeats v):
  //   21000 8808 14*0 21000 8808 204000 400 4*0 21000 8808 104000 400 4*0 21000 8808 24000 200008 400 0 0
  //   0 21000 8808 24000 100008 400 0 0 0 21000 8808 24000 80010 400 0 0 0 21000 8808 24000 40010 400 0 0
  //   0 21000 8808 60000 200008 400 0 0 0 21000 8808 60000 80010 400 0 0 0 21000 8808 180000 400 4*0 21000
  //   8808 200004 400 4*0 21000 8808 2 400 4*0 21000 8808 1 400 4*0 21000 8808 6000 400 4*0 21000 8808 6*0
  //   21000 8808 6*0 21000 8808 6*0 21000 8808 200020 10000 400 0 0 0 21000 8808 200060 10000 400 0 0 0
  //   21000 8808 2000a0 10000 400 0 0 0 21000 8808 2000e0 10000 400 0 0 0 21000 8808 200120 10000 400 0 0
  //   0 21000 8808 200160 10000 400 0 0 0 21000 8808 2001a0 10000 400 0 0 0 21000 8808 2001e0 10000 400 0
  //   0 0 21000 8808 200220 10000 400 0 0 0 21000 8808 200260 10000 400 0 0 0 21000 8808 10000 400 28*0
  //   21000 8808 14*0 21000 8808 204000 400 4*0 21000 8808 104000 400 4*0 21000 8808 24000 200008 400 0 0
  //   0 21000 8808 24000 100008 400 0 0 0 21000 8808 24000 80010 400 0 0 0 21000 8808 24000 40010 400 0 0
  //   0 21000 8808 60000 200008 400 0 0 0 21000 8808 60000 80010 400 0 0 0 21000 8808 180000 400 4*0 21000
  //   8808 200004 400 4*0 21000 8808 2 400 4*0 21000 8808 1 400 4*0 21000 8808 6000 400 4*0 21000 8808
  //   6000 400 4*0 21000 8808 6*0 21000 8808 6*0 21000 8808 200020 10000 400 0 0 0 21000 8808 200060 10000
  //   400 0 0 0 21000 8808 2000a0 10000 400 0 0 0 21000 8808 2000e0 10000 400 0 0 0 21000 8808 200120
  //   10000 400 0 0 0 21000 8808 200160 10000 400 0 0 0 21000 8808 2001a0 10000 400 0 0 0 21000 8808
  //   2001e0 10000 400 0 0 0 21000 8808 200220 10000 400 0 0 0 21000 8808 200260 10000 400 0 0 0 21000
  //   8808 10000 400 28*0 21000 8808 14*0 21000 8808 204000 400 4*0 21000 8808 104000 400 4*0 21000 8808
  //   24000 200008 400 0 0 0 21000 8808 24000 100008 400 0 0 0 21000 8808 24000 80010 400 0 0 0 21000 8808
  //   24000 40010 400 0 0 0 21000 8808 60000 200008 400 0 0 0 21000 8808 60000 80010 400 0 0 0 21000 8808
  //   180000 400 4*0 21000 8808 200004 400 4*0 21000 8808 2 400 4*0 21000 8808 1 400 4*0 21000 8808 6000
  //   400 4*0 21000 8808 6*0 21000 8808 6000 400 4*0 21000 8808 6*0 21000 8808 200020 10000 400 0 0 0
  //   21000 8808 200060 10000 400 0 0 0 21000 8808 2000a0 10000 400 0 0 0 21000 8808 2000e0 10000 400 0 0
  //   0 21000 8808 200120 10000 400 0 0 0 21000 8808 200160 10000 400 0 0 0 21000 8808 2001a0 10000 400 0
  //   0 0 21000 8808 2001e0 10000 400 0 0 0 21000 8808 200220 10000 400 0 0 0 21000 8808 200260 10000 400
  //   0 0 0 21000 8808 10000 400 28*0 21000 8808 14*0 21000 8808 204000 400 4*0 21000 8808 104000 400 4*0
  //   21000 8808 24000 200008 400 0 0 0 21000 8808 24000 100008 400 0 0 0 21000 8808 24000 80010 400 0 0 0
  //   21000 8808 24000 40010 400 0 0 0 21000 8808 60000 200008 400 0 0 0 21000 8808 60000 80010 400 0 0 0
  //   21000 8808 180000 400 4*0 21000 8808 200004 400 4*0 21000 8808 2 400 4*0 21000 8808 1 400 4*0 21000
  //   8808 6000 400 4*0 21000 8808 6000 400 4*0 21000 8808 6000 400 4*0 21000 8808 6*0 21000 8808 200020
  //   10000 400 0 0 0 21000 8808 200060 10000 400 0 0 0 21000 8808 2000a0 10000 400 0 0 0 21000 8808
  //   2000e0 10000 400 0 0 0 21000 8808 200120 10000 400 0 0 0 21000 8808 200160 10000 400 0 0 0 21000
  //   8808 2001a0 10000 400 0 0 0 21000 8808 2001e0 10000 400 0 0 0 21000 8808 200220 10000 400 0 0 0
  //   21000 8808 200260 10000 400 0 0 0 21000 8808 10000 400 28*0 21000 8808 14*0 21000 8808 204000 400
  //   4*0 21000 8808 104000 400 4*0 21000 8808 24000 200008 400 0 0 0 21000 8808 24000 100008 400 0 0 0
  //   21000 8808 24000 80010 400 0 0 0 21000 8808 24000 40010 400 0 0 0 21000 8808 60000 200008 400 0 0 0
  //   21000 8808 60000 80010 400 0 0 0 21000 8808 180000 400 4*0 21000 8808 200004 400 4*0 21000 8808 2
  //   400 4*0 21000 8808 1 400 4*0 21000 8808 6000 400 4*0 21000 8808 6*0 21000 8808 6*0 21000 8808 6000
  //   400 4*0 21000 8808 200020 10000 400 0 0 0 21000 8808 200060 10000 400 0 0 0 21000 8808 2000a0 10000
  //   400 0 0 0 21000 8808 2000e0 10000 400 0 0 0 21000 8808 200120 10000 400 0 0 0 21000 8808 200160
  //   10000 400 0 0 0 21000 8808 2001a0 10000 400 0 0 0 21000 8808 2001e0 10000 400 0 0 0 21000 8808
  //   200220 10000 400 0 0 0 21000 8808 200260 10000 4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
endmodule
